# Fritzing sketch Reaction game (saved by Fritzing 0.9.9b)
circuit board: 8.46667cm x 5.64444cm
breadboards: 1

parts:
  Onderdeel1 = Arduino Uno (Rev3)
  S1 = Pushbutton [package="[THT]"]
  R1 = Resistor [tolerance=±5% power=0.25 resistance=220 package=THT]
  U1 = 74HC595 [package="DIP16 [THT]"]
  U2 = 7-SEGMENT-DISPLAY [package=7-segment-display]
  R2 = Resistor [tolerance=±5% power=0.25 resistance=220 package=THT]
  R3 = Resistor [tolerance=±5% power=0.25 resistance=220 package=THT]
  LED1 = smd LED [color="Red (633nm)" package="0603 [SMD]"]
  R4 = Resistor [tolerance=±5% power=0.25 resistance=220 package=THT]
  LED2 = RGB LED (com. cathode, rgb) [package="5 mm [THT]"]
  R5 = Resistor [tolerance=±5% power=0.25 resistance=220 package=THT]
  R6 = Resistor [tolerance=±5% power=0.25 resistance=220 package=THT]
  R7 = Resistor [tolerance=±5% power=0.25 resistance=220 package=THT]
  J1 = Piezo Speaker
  R8 = Resistor [tolerance=±5% power=0.25 resistance=220 package=THT]

nets:
  N1: Onderdeel1.D8, R4.Pin_1
  N2: Onderdeel1.D12/MISO, R7.Pin_1
  N3: Onderdeel1.D13/SCK, R8.Pin_1
  N4: Onderdeel1.D2, S1.Pin_3, S1.Pin_4
  N5: Onderdeel1.D3_PWM, U1.DS
  N6: Onderdeel1.D4, U1.ST_CP
  N7: Onderdeel1.D5_PWM, U1.SH_CP
  N8: Onderdeel1.D6_PWM, R5.Pin_1
  N9: Onderdeel1.D7, R6.Pin_1
  5V: Onderdeel1.5V, U1.MR, U1.VCC
  GND: Onderdeel1.GND, R1.Pin_0, U1.GND, U1.OE, R2.Pin_0, R3.Pin_1, LED1.anode, LED2.common_cathode, J1.pin1
  N10: S1.Pin_1, S1.Pin_2, R1.Pin_1
  N11: U1.Q1, U2.A
  N12: U1.Q2, U2.G2
  N13: U1.Q3, U2.G
  N14: U1.Q4, U2.E
  N15: U1.Q5, U2.G1
  N16: U1.Q6, U2.DP
  N17: U1.Q0, U2.D
  N18: U2.C, R3.Pin_0
  N19: U2.F, R2.Pin_1
  N20: LED1.cathode, R4.Pin_0
  N21: LED2.green_anode, R6.Pin_0
  N22: LED2.blue_anode, R7.Pin_0
  N23: J1.pin2, R8.Pin_0

// code stored in the sketch: reactie_spel_final2.ino
#include <Wire.h>
#include <LiquidCrystal_I2C.h>
#include "pitches.h"

#define SHOOT_LED 8 //IO pins
#define LIVE_3 9
#define LIVE_2 10
#define LIVE_1 11
#define BUTTON 2
#define LEDR 6
#define LEDG 7
#define LEDB 12
#define SPEAKER 13
#define DATA 3
#define LATCH 4
#define CLOCK 5
#define PUNT 1

#define minimum 1000 //Random times
#define maximum 5000

#define a 32 //Seven segment displays
#define b 64
#define c 2
#define d 4
#define e 128
#define f 16
#define g 8
#define ONE b+c
#define TWO a+b+g+e+d
#define THREE a+b+g+c+d
#define FOUR f+g+b+c
#define FIVE a+f+g+c+d
#define SIX a+f+g+c+d+e
#define SEVEN a+b+c
#define EIGHT a+b+c+d+e+f+g
#define NINE d+c+g+f+a+b
#define SAD b+d+f

unsigned long TimeLedOn;
unsigned long TimeButtonPressed;
bool LevelUp = false;
int GameMode = 0;
byte SevenSegmentDisplayData = 0;
int level = 1;

int StartCycle = 0;
int score = 0;
int MaxReactionTime = 1000;
int Lives = 3;
bool LCDStart = false;

LiquidCrystal_I2C lcd(0x3F, 16, 2); // set the LCD address to 0x27 for a 16 chars and 2 line display






// Two things need to be created: the array for the notes of the melody (in order)
// and the duration of each (think of it like sheet music in two parts)

// BOTH ARRAYS MUST BE THE SAME SIZE!

// The melody array
int gameOverMelodyNotes[] = {
  NOTE_FS3, NOTE_GS3, NOTE_A3, NOTE_E3, NOTE_FS3, NOTE_C4, NOTE_B2
  , NOTE_B2, NOTE_B2
};

// The note duration, 8 = 8th note, 4 = quarter note, etc.
int gameOverMelodyDuration[] = {
  8, 8, 8, 8, 4, 4, 2
  , 4, 4
};
// determine the length of the arrays to use in the loop iteration
int songLength = sizeof(gameOverMelodyNotes) / sizeof(gameOverMelodyNotes[0]);






void setup() {
  lcd.init();       // initialize the lcd
  lcd.backlight();
  pinMode(BUTTON, INPUT_PULLUP);
  pinMode(SHOOT_LED, OUTPUT);
  pinMode(LIVE_1, OUTPUT);
  pinMode(LIVE_2, OUTPUT);
  pinMode(LIVE_3, OUTPUT);
  pinMode(LATCH, OUTPUT);
  pinMode(DATA, OUTPUT);
  pinMode(CLOCK, OUTPUT);
  pinMode(LEDR, OUTPUT);
  pinMode(LEDG, OUTPUT);
  pinMode(LEDB, OUTPUT);
  pinMode(SPEAKER, OUTPUT);
  Serial.begin(9600);
}


void resetled() {
  digitalWrite(LIVE_3, LOW);
  digitalWrite(LIVE_2, LOW);
  digitalWrite(LIVE_1, LOW);
  digitalWrite(SHOOT_LED, LOW);
}

void loop() {
  int buttonState = digitalRead(BUTTON);
  if (GameMode == 0) {
    if (LCDStart == false) {
      lcd.clear();
      lcd.setCursor(0, 0);
      lcd.print("PRESS THE BUTTON");
      lcd.setCursor(4, 1);
      lcd.print("TO START");
      LCDStart = true;
    }

    StartCycle += 1;
    if (StartCycle == 3) {
      StartCycle = 0;
    }
    level = 1;
    if (StartCycle == 0) {
      digitalWrite(LIVE_3, LOW);
      digitalWrite(LIVE_1, HIGH);
      digitalWrite(SHOOT_LED, HIGH);
      RGB_color(0, 255, 255); // Light blue


      SevenSegmentDisplayData = PUNT;
    }
    if (StartCycle == 1) {
      digitalWrite(LIVE_1, LOW);
      digitalWrite(LIVE_2, HIGH);
      RGB_color(255, 0, 255); // Magenta

    }
    if (StartCycle == 2) {
      digitalWrite(LIVE_2, LOW);
      digitalWrite(LIVE_3, HIGH);
      digitalWrite(SHOOT_LED, LOW);
      RGB_color(255, 255, 0); // Yellow
      SevenSegmentDisplayData = 0;
    }

    delay(300);

    if (buttonState == LOW) {
      GameMode = 1;
      resetled();
      lcd.clear();
      LCDStart = false;
      delay(1000);
    }
  }

  if (GameMode == 1) {
    resetled();
    if (Lives == 3) {
      RGB_color(0, 255, 0);
      digitalWrite(LIVE_1, HIGH);
      digitalWrite(LIVE_2, HIGH);
      digitalWrite(LIVE_3, HIGH);

    }
    if (Lives == 2) {
      RGB_color(255, 255, 0);
      digitalWrite(LIVE_2, HIGH);
      digitalWrite(LIVE_3, HIGH);
    }
    if (Lives == 1) {
      RGB_color(255, 0, 0);
      digitalWrite(LIVE_3, HIGH);

    }

    int RandomTime = random(minimum, maximum);

    int TimeReaction = 10;
    bool vroeg = false;
    float LevelTime = level * 100;
    TimeLedOn = millis();
    if (level == 1) {
      SevenSegmentDisplayData = ONE;
    }
    if (score == 3) {
      level = 2; //0.8
      SevenSegmentDisplayData = TWO;
      levelup();
    }
    if (score == 6) {
      level = 3; //0.7
      SevenSegmentDisplayData = THREE;
      levelup();
    }
    if (score == 9) {
      level = 4; //0.6
      SevenSegmentDisplayData = FOUR;
      levelup();
    }
    if (score == 13) {
      level = 5; //0.5
      SevenSegmentDisplayData = FIVE;
      levelup();
    }
    if (score == 17) {
      level = 6; //0.4
      SevenSegmentDisplayData = SIX;
      levelup();
    }
    if (score == 22) {
      level = 7; //0.3
      SevenSegmentDisplayData = SEVEN;
      levelup();
    }
    if (score == 27) {
      level = 8; //0.2
      SevenSegmentDisplayData = EIGHT;
      levelup();
    }
    if (score == 33) {
      level = 9; //0.1
      SevenSegmentDisplayData = NINE;
      levelup();
    }

    lcd.clear();
    lcd.setCursor(0, 0);
    lcd.print("PRESS THE BUTTON");
    lcd.setCursor(0, 1);
    lcd.print("IF RED LED IS ON");
    if (LevelUp == true) {
      delay(2000);
      LevelUp = false;
    }

    while (TimeReaction <= RandomTime && vroeg == false) {

      TimeReaction = millis() - TimeLedOn;

      buttonState = digitalRead(BUTTON);

      if (buttonState == LOW) {
        Lives -= 1;
        Serial.println("te vroeg!");
        lcd.clear();
        lcd.setCursor(0, 0);
        lcd.print("TE VROEG");
        lcd.setCursor(0, 1);
        lcd.print("D:");
        RGB_color(0, 255, 255);
        vroeg = true;
        delay(2000);
      }
    }



    if (buttonState == HIGH && vroeg == false) {
      digitalWrite(SHOOT_LED, HIGH);
      TimeLedOn = millis();
      while (buttonState == HIGH) {
        buttonState = digitalRead(BUTTON);
      }
      TimeButtonPressed = millis();
      TimeReaction = TimeButtonPressed - TimeLedOn;


      if (TimeReaction <= MaxReactionTime - LevelTime) {
        Serial.println("RAAK!");
        RGB_color(0, 255, 255);
        lcd.clear();
        lcd.setCursor(0, 0);
        lcd.print("RAAK!");
        lcd.setCursor(0, 1);
        lcd.print(":D");
      }

      if (TimeReaction >= MaxReactionTime - LevelTime) {
        Lives -= 1;
        Serial.println("te laat!");
        lcd.clear();
        lcd.setCursor(0, 0);
        lcd.print("TE LAAT");
        lcd.setCursor(0, 1);
        lcd.print("D:");
        RGB_color(0, 255, 255);
        RGB_color(0, 255, 255);
      }
      delay(2000);
    }
    if (vroeg == false) {
      Serial.println("Dit koste: ");
      Serial.print(TimeReaction * 0.001);
      Serial.println(" Seconden");
      lcd.clear();
      lcd.setCursor(0, 0);
      lcd.print("Dit koste:");
      lcd.setCursor(0, 1);
      lcd.print(TimeReaction * 0.001);
      lcd.setCursor(13, 1);
      lcd.print("sec");
      delay(2000);
    }
    vroeg = false;
    LevelUp = false;
    score += 1;
    if (Lives == 0) {
      GameMode = 2;
    }


  }


  if (GameMode == 2) {
    digitalWrite(SHOOT_LED, HIGH);
    long highscore = score + 15;
    Serial.println("WOW, Je hebt wel ");
    Serial.print(score);
    Serial.print(" punten, dat is bijna de high score  >---");
    Serial.print(highscore);
    Serial.print("---<");
    GameMode = 0;
    Lives = 3;
    SevenSegmentDisplayData = SAD;
    updateShiftRegister();
    music();

    lcd.clear();
    lcd.setCursor(0, 0);
    lcd.print("Helaas");
    lcd.setCursor(5, 1);
    lcd.print("D:");
    delay(1500);
    lcd.clear();
    lcd.setCursor(0, 0);
    lcd.print("Je hebt al");
    lcd.setCursor(0, 1);
    lcd.print("je Levens");
    delay(2000);
    lcd.clear();
    lcd.setCursor(0, 0);
    lcd.print("verloren");
    delay(1500);
    lcd.clear();
    lcd.setCursor(0, 0);
    lcd.print("je score is:");
    lcd.setCursor(4, 1);
    lcd.print(score);
    delay(1500);
    lcd.clear();
    lcd.setCursor(0, 0);
    lcd.print("Highscore is:");
    lcd.setCursor(4, 1);
    lcd.print(score + 3);
    delay(1500);
    score = 0;

  }





  updateShiftRegister();
}

void updateShiftRegister()
{
  digitalWrite(LATCH, LOW);
  shiftOut(DATA, CLOCK, LSBFIRST, SevenSegmentDisplayData);
  digitalWrite(LATCH, HIGH);
}

void RGB_color(int red_light_value, int green_light_value, int blue_light_value)
{
  analogWrite(LEDR, red_light_value);
  analogWrite(LEDG, green_light_value);
  analogWrite(LEDB, blue_light_value);
}

void music() {
  for (int thisNote = 0; thisNote < songLength; thisNote++) {
    // determine the duration of the notes that the computer understands
    // divide 1000 by the value, so the first note lasts for 1000/8 milliseconds
    int duration = 1000 / gameOverMelodyDuration[thisNote];
    tone(SPEAKER, gameOverMelodyNotes[thisNote], duration);
    // pause between notes
    int pause = duration * 1.3;
    delay(pause);
    // stop the tone
    noTone(SPEAKER);
  }
}

void levelup() {
  lcd.clear();
  updateShiftRegister();
  lcd.setCursor(1, 0);
  lcd.print("-LEVEL UP-");
  tone(13, NOTE_B2, 500);
  delay(400);
  lcd.setCursor(1, 0);
  lcd.print("*LEVEL UP*");
  delay(400);
  lcd.setCursor(1, 0);
  lcd.print("|LEVEL UP|");
  delay(400);
  lcd.setCursor(1, 0);
  lcd.print("*LEVEL UP*");
  delay(400);
  lcd.setCursor(1, 0);
  lcd.print("-LEVEL UP-");
  delay(400);
  lcd.setCursor(1, 0);
  lcd.print("*LEVEL UP*");
  delay(400);
  lcd.setCursor(1, 0);
  lcd.print("|LEVEL UP|");
  delay(400);
  lcd.setCursor(1, 0);
  lcd.print("*LEVEL UP*");
  tone(13, NOTE_A1, 500);
  delay(1000);
  LevelUp = true;
}
